// Logisim project main.circ as structural Verilog: 8 circuits, main circuit main
module main (
);

  wire and_3_out, and_4_out, and_5_out, and_6_out, and_7_out, and_8_out, and_9_out, and_10_out, and_11_out,
       cdm_16_1_p4, cdm_16_1_p5, cdm_16_1_p7, cdm_16_1_p8, cdm_16_1_p9, cdm_16_1_p10, cdm_16_1_p12,
       cdm_16_1_p13, cdm_16_1_p14, cdm_16_1_p15, cdm_16_1_p16, cdm_16_1_p17, cl, comparator_2_eq,
       comparator_3_eq, comparator_4_eq, comparator_5_eq, comparator_6_eq, comparator_7_eq, comparator_8_eq,
       comparator_9_eq, decoder_1_out0, decoder_1_out1, I_Osel, IAck, In_out, interruptarbiter_1_vec, IRQ,
       kb_ctrl, kb_ready, mem, nand_1_out, not_1_out, not_2_out, or_1_out, RAM, Rset, start, ter_ctrl, upd,
       val, word;
  wire [0:0] register_1_q;
  wire [1:1] comparator_1_eq;
  wire [5:0] vec;
  wire [6:0] kb_data, ter_data;
  wire [7:0] born, cadr, ladr, sur, surv;
  wire [15:0] address_bus, bit_extender_2_out, cdm_16_1_p22, cdm_16_1_p23, data_bus;
  wire [15:1] register_2_q, register_3_q, register_8_q;
  wire [15:8] register_4_q, register_5_q, register_6_q, register_7_q;
  wire [31:0] videobuffer_1_out_9, videobuffer_1_out_10, videobuffer_1_out_11, videobuffer_1_out_12,
       videobuffer_1_out_13, videobuffer_1_out_14, videobuffer_1_out_15, videobuffer_1_out_16,
       videobuffer_1_out_17, videobuffer_1_out_18, videobuffer_1_out_19, videobuffer_1_out_20,
       videobuffer_1_out_21, videobuffer_1_out_22, videobuffer_1_out_23, videobuffer_1_out_24,
       videobuffer_1_out_25, videobuffer_1_out_26, videobuffer_1_out_27, videobuffer_1_out_28,
       videobuffer_1_out_29, videobuffer_1_out_30, videobuffer_1_out_31, videobuffer_1_out_32,
       videobuffer_1_out_33, videobuffer_1_out_34, videobuffer_1_out_35, videobuffer_1_out_36,
       videobuffer_1_out_37, videobuffer_1_out_38, videobuffer_1_out_39, videobuffer_1_out_40;

  // Probe on cdm_16_1_p14
  // Probe on cdm_16_1_p13
  // Probe on cdm_16_1_p12
  // Probe on cdm_16_1_p9
  // Probe on cdm_16_1_p8
  // Probe on cdm_16_1_p7
  // Probe on cdm_16_1_p5
  // Probe on cdm_16_1_p4
  // CdM_16 cdm_16_1: pin names not known; wires that end beside it: IRQ, vec, IAck, cdm_16_1_p4, cdm_16_1_p5, cl, cdm_16_1_p7, cdm_16_1_p8, cdm_16_1_p9, cdm_16_1_p10, cdm_16_1_p10, cdm_16_1_p12, cdm_16_1_p13, cdm_16_1_p14, cdm_16_1_p15, cdm_16_1_p16, cdm_16_1_p17, mem, In_out, word, address_bus, cdm_16_1_p22, cdm_16_1_p23
  // Probe on vec
  and and_1 (I_Osel, not_1_out, cl, mem);
  not not_1 (not_1_out, nand_1_out);
  and and_2 (RAM, nand_1_out, mem);
  Bit_Extender #(.in_width(16), .out_width(7)) bit_extender_1 (.in(data_bus), .out(ter_data));
  LED led_1 (.in(start));
  LED led_2 (.in(upd));
  // Probe on cdm_16_1_p15
  // Probe on cdm_16_1_p16
  // Probe on cdm_16_1_p17
  assign data_bus = not_2_out ? cdm_16_1_p22 : 16'bz;  // Controlled_Buffer controlled_buffer_1
  not not_2 (not_2_out, In_out);
  assign cdm_16_1_p23 = In_out ? data_bus : 16'bz;  // Controlled_Buffer controlled_buffer_2
  nand nand_1 (nand_1_out, address_bus[8], address_bus[9], address_bus[10], address_bus[11], address_bus[12], address_bus[13], address_bus[14], address_bus[15]);
  Comparator comparator_1 (.a(address_bus[7:0]), .b(8'h2), .eq(comparator_1_eq[1]));  // open: gt, lt
  Comparator comparator_2 (.a(address_bus[7:0]), .b({8{1'b0}}), .eq(comparator_2_eq));  // open: gt, lt
  Register #(.width(1), .trigger("falling")) register_1 (
    .D(data_bus[0]), .en(decoder_1_out0), .Q(register_1_q[0]), .clk(cl), .clr(Rset));
  videobuffer videobuffer_1 (
    .line_adr(ladr), .cell_adr(cadr), .out_9(videobuffer_1_out_9), .out_10(videobuffer_1_out_10),
    .out_11(videobuffer_1_out_11), .out_12(videobuffer_1_out_12), .out_13(videobuffer_1_out_13),
    .out_14(videobuffer_1_out_14), .out_15(videobuffer_1_out_15), .out_16(videobuffer_1_out_16),
    .out_17(videobuffer_1_out_17), .out_18(videobuffer_1_out_18), .out_19(videobuffer_1_out_19),
    .out_20(videobuffer_1_out_20), .out_21(videobuffer_1_out_21), .out_22(videobuffer_1_out_22),
    .out_23(videobuffer_1_out_23), .out_24(videobuffer_1_out_24), .out_25(videobuffer_1_out_25),
    .out_26(videobuffer_1_out_26), .out_27(videobuffer_1_out_27), .out_28(videobuffer_1_out_28),
    .out_29(videobuffer_1_out_29), .out_30(videobuffer_1_out_30), .out_31(videobuffer_1_out_31),
    .out_32(videobuffer_1_out_32), .out_33(videobuffer_1_out_33), .out_34(videobuffer_1_out_34),
    .out_35(videobuffer_1_out_35), .out_36(videobuffer_1_out_36), .out_37(videobuffer_1_out_37),
    .out_38(videobuffer_1_out_38), .out_39(videobuffer_1_out_39), .out_40(videobuffer_1_out_40), .sur(surv),
    .born(born), .cl(cl), .start_stop(start), .update(upd), .val(val));
  DotMatrix #(.inputtype("row"), .matrixcols(32), .matrixrows(32)) dotmatrix_1 (
    .row0(videobuffer_1_out_9), .row1(videobuffer_1_out_10), .row2(videobuffer_1_out_11),
    .row3(videobuffer_1_out_12), .row4(videobuffer_1_out_13), .row5(videobuffer_1_out_14),
    .row6(videobuffer_1_out_15), .row7(videobuffer_1_out_16), .row8(videobuffer_1_out_17),
    .row9(videobuffer_1_out_18), .row10(videobuffer_1_out_19), .row11(videobuffer_1_out_20),
    .row12(videobuffer_1_out_21), .row13(videobuffer_1_out_22), .row14(videobuffer_1_out_23),
    .row15(videobuffer_1_out_24), .row16(videobuffer_1_out_25), .row17(videobuffer_1_out_26),
    .row18(videobuffer_1_out_27), .row19(videobuffer_1_out_28), .row20(videobuffer_1_out_29),
    .row21(videobuffer_1_out_30), .row22(videobuffer_1_out_31), .row23(videobuffer_1_out_32),
    .row24(videobuffer_1_out_33), .row25(videobuffer_1_out_34), .row26(videobuffer_1_out_35),
    .row27(videobuffer_1_out_36), .row28(videobuffer_1_out_37), .row29(videobuffer_1_out_38),
    .row30(videobuffer_1_out_39), .row31(videobuffer_1_out_40));
  Clock clock_1 (.out(cl));
  or or_1 (or_1_out, comparator_1_eq[1], comparator_2_eq);
  and and_3 (and_3_out, or_1_out, I_Osel);
  Decoder #(.select(2), .disabled(0)) decoder_1 (
    .out0(decoder_1_out0), .out1(decoder_1_out1), .out2(ter_ctrl), .out3(kb_ctrl),
    .sel({comparator_1_eq[1], In_out}), .en(and_3_out));
  assign data_bus = kb_ctrl ? bit_extender_2_out : 16'bz;  // Controlled_Buffer controlled_buffer_3
  assign data_bus = decoder_1_out1 ? {kb_ready, {14{1'b0}}, register_1_q[0]} : 16'bz;  // Controlled_Buffer controlled_buffer_4
  TTY #(.rows(16), .cols(80), .trigger("falling")) tty_1 (.data(ter_data), .clk(cl), .we(ter_ctrl), .clr(Rset));
  assign bit_extender_2_out = {{9{1'b0}}, kb_data};  // Bit_Extender bit_extender_2
  // Probe on address_bus
  // Debugger debugger_1: pin names not known
  assign vec = interruptarbiter_1_vec ? 6'b000101 : 6'bz;  // Controlled_Buffer controlled_buffer_5
  InterruptArbiter interruptarbiter_1 (
    .IReq_2(IRQ), .IAck(IAck), .IReq(1'b0), .vec(interruptarbiter_1_vec), .req(and_4_out), .done(kb_ctrl),
    .clock(cl));  // open: IAck_2
  and and_4 (and_4_out, kb_ready, register_1_q[0]);
  Keyboard #(.trigger("falling")) keyboard_1 (.clk(cl), .re(kb_ctrl), .clr(Rset), .avail(kb_ready), .data(kb_data));
  // RAM ram_1: pin names not known; wires that end beside it: address_bus, word, RAM, mem, cl, In_out, Rset, data_bus
  Button button_1 (.out(Rset));
  // Probe on data_bus
  Comparator comparator_3 (.a(address_bus[7:0]), .b(8'h4), .eq(comparator_3_eq));  // open: gt, lt
  Comparator comparator_4 (.a(address_bus[7:0]), .b(8'h6), .eq(comparator_4_eq));  // open: gt, lt
  Comparator comparator_5 (.a(address_bus[7:0]), .b(8'h8), .eq(comparator_5_eq));  // open: gt, lt
  Comparator comparator_6 (.a(address_bus[7:0]), .b(8'ha), .eq(comparator_6_eq));  // open: gt, lt
  Comparator comparator_7 (.a(address_bus[7:0]), .b(8'hc), .eq(comparator_7_eq));  // open: gt, lt
  Comparator comparator_8 (.a(address_bus[7:0]), .b(8'he), .eq(comparator_8_eq));  // open: gt, lt
  Comparator comparator_9 (.a(address_bus[7:0]), .b(8'h10), .eq(comparator_9_eq));  // open: gt, lt
  // Probe on data_bus
  Register #(.width(16), .trigger("falling")) register_2 (
    .D(data_bus), .en(and_5_out), .Q({register_2_q, start}), .clk(cl), .clr(Rset));
  and and_5 (and_5_out, comparator_3_eq, I_Osel);
  Register #(.width(16), .trigger("falling")) register_3 (
    .D(data_bus), .en(and_6_out), .Q({register_3_q, upd}), .clk(cl), .clr(Rset));
  and and_6 (and_6_out, comparator_4_eq, I_Osel);
  Register #(.width(16), .trigger("falling")) register_4 (
    .D(data_bus), .en(and_7_out), .Q({register_4_q, born}), .clk(cl), .clr(Rset));
  and and_7 (and_7_out, comparator_5_eq, I_Osel);
  Register #(.width(16), .trigger("falling")) register_5 (
    .D(data_bus), .en(and_8_out), .Q({register_5_q, sur}), .clk(cl), .clr(Rset));
  and and_8 (and_8_out, comparator_6_eq, I_Osel);
  Register #(.width(16), .trigger("falling")) register_6 (
    .D(data_bus), .en(and_9_out), .Q({register_6_q, ladr}), .clk(cl), .clr(Rset));
  and and_9 (and_9_out, comparator_7_eq, I_Osel);
  Register #(.width(16), .trigger("falling")) register_7 (
    .D(data_bus), .en(and_10_out), .Q({register_7_q, cadr}), .clk(cl), .clr(Rset));
  and and_10 (and_10_out, comparator_8_eq, I_Osel);
  Register #(.width(16), .trigger("falling")) register_8 (
    .D(data_bus), .en(and_11_out), .Q({register_8_q, val}), .clk(cl), .clr(Rset));
  and and_11 (and_11_out, comparator_9_eq, I_Osel);

  // Other names for the same wires on the sheet: read = In_out; I_Oadr[7:0] = address_bus[7:0];
  //   I_Odat[15:0] = data_bus

  // Notes on the sheet:
  //   r7/fp
  //   r6
  //   r5
  //   r4
  //   r3
  //   r2
  //   r1
  //   r0
  //   memory-mapped I/O
  //   pc
  //   sp
  //   ps
  //   start/stop
  //   out_ctr
  //   born
  //   sur
  //   line_addr
  //   cell_addr
  //   val
endmodule

module \cell  (
  input  clock,
  input  out_force,
  input  out_control,
  input  [7:0] around,
  input  [7:0] born_rule,
  input  [7:0] survival_rule,
  output state
);

  wire and_1_out, check_rules_1_born, check_rules_1_survive, controlled_buffer_1_out,
       controlled_inverter_1_out, or_1_out;
  wire [3:0] bitadder_1_out;

  assign controlled_buffer_1_out = out_control ? out_force : 1'bz;  // Controlled_Buffer controlled_buffer_1
  assign controlled_inverter_1_out = out_control ? ~out_force : 1'bz;  // Controlled_Inverter controlled_inverter_1
  BitAdder bitadder_1 (.in0(around), .out(bitadder_1_out));
  D_Flip_Flop d_ff_1 (
    .clk(clock), .D(or_1_out), .Q(state), .preset(controlled_buffer_1_out), .reset(controlled_inverter_1_out));  // open: Qn, en
  check_rules check_rules_1 (
    .count(bitadder_1_out), .born_rule(born_rule), .survival_rule(survival_rule), .Born(check_rules_1_born),
    .survive(check_rules_1_survive));
  and and_1 (and_1_out, state, check_rules_1_survive);
  or or_1 (or_1_out, check_rules_1_born, and_1_out);
endmodule

module line (
  input  [7:0] survival_rules,
  input  [7:0] born_rules,
  input  clock,
  input  ctrl,
  input  val,
  input  [7:0] cell_adr,
  input  [31:0] up,
  input  [31:0] down,
  output [31:0] output_up,
  output [31:0] output_down,
  output [31:0] output_main
);

  wire a0, a1, a2, a3, a4, a5, a6, a7, a8, a9, a10, a11, a12, a13, a14, a15, a16, a17, a18, a19, a20, a21,
       a22, a23, a24, a25, a26, a27, a28, a29, a30, a31, u0, u1, u2, u3, u4, u5, u6, u7, u8, u9, u10, u11,
       u12, u13, u14, u15, u16, u17, u18, u19, u20, u21, u22, u23, u24, u25, u26, u27, u28, u29, u30, u31;

  Demultiplexer #(.select(5), .enable("false")) demultiplexer_1 (
    .out0(u31), .out1(u30), .out2(u29), .out3(u28), .out4(u27), .out5(u26), .out6(u25), .out7(u24),
    .out8(u23), .out9(u22), .out10(u21), .out11(u20), .out12(u19), .out13(u18), .out14(u17), .out15(u16),
    .out16(u15), .out17(u14), .out18(u13), .out19(u12), .out20(u11), .out21(u10), .out22(u9), .out23(u8),
    .out24(u7), .out25(u6), .out26(u5), .out27(u4), .out28(u3), .out29(u2), .out30(u1), .out31(u0), .in(val),
    .sel(cell_adr[4:0]));
  Demultiplexer #(.select(5), .enable("false")) demultiplexer_2 (
    .out0(a31), .out1(a30), .out2(a29), .out3(a28), .out4(a27), .out5(a26), .out6(a25), .out7(a24),
    .out8(a23), .out9(a22), .out10(a21), .out11(a20), .out12(a19), .out13(a18), .out14(a17), .out15(a16),
    .out16(a15), .out17(a14), .out18(a13), .out19(a12), .out20(a11), .out21(a10), .out22(a9), .out23(a8),
    .out24(a7), .out25(a6), .out26(a5), .out27(a4), .out28(a3), .out29(a2), .out30(a1), .out31(a0),
    .in(ctrl), .sel(cell_adr[4:0]));
  \cell  cell_1 (
    .around({up[0], down[0], up[1], down[1], up[31], down[31], output_down[31], output_down[1]}),
    .born_rule(born_rules), .survival_rule(survival_rules), .clock(clock), .state(output_down[0]),
    .out_force(u0), .out_control(a0));
  \cell  cell_2 (
    .around({up[7], down[7], up[8], down[8], up[9], down[9], output_down[7], output_down[9]}),
    .born_rule(born_rules), .survival_rule(survival_rules), .clock(clock), .state(output_down[8]),
    .out_force(u8), .out_control(a8));
  \cell  cell_3 (
    .around({up[15], down[15], up[16], down[16], up[17], down[17], output_down[15], output_down[17]}),
    .born_rule(born_rules), .survival_rule(survival_rules), .clock(clock), .state(output_down[16]),
    .out_force(u16), .out_control(a16));
  \cell  cell_4 (
    .around({up[23], down[23], up[24], down[24], up[25], down[25], output_down[23], output_down[25]}),
    .born_rule(born_rules), .survival_rule(survival_rules), .clock(clock), .state(output_down[24]),
    .out_force(u24), .out_control(a24));
  \cell  cell_5 (
    .around({up[0], down[0], up[1], down[1], up[2], down[2], output_down[0], output_down[2]}),
    .born_rule(born_rules), .survival_rule(survival_rules), .clock(clock), .state(output_down[1]),
    .out_force(u1), .out_control(a1));
  \cell  cell_6 (
    .around({up[8], down[8], up[9], down[9], up[10], down[10], output_down[8], output_down[10]}),
    .born_rule(born_rules), .survival_rule(survival_rules), .clock(clock), .state(output_down[9]),
    .out_force(u9), .out_control(a9));
  \cell  cell_7 (
    .around({up[16], down[16], up[17], down[17], up[18], down[18], output_down[16], output_down[18]}),
    .born_rule(born_rules), .survival_rule(survival_rules), .clock(clock), .state(output_down[17]),
    .out_force(u17), .out_control(a17));
  \cell  cell_8 (
    .around({up[24], down[24], up[25], down[25], up[26], down[26], output_down[24], output_down[26]}),
    .born_rule(born_rules), .survival_rule(survival_rules), .clock(clock), .state(output_down[25]),
    .out_force(u25), .out_control(a25));
  \cell  cell_9 (
    .around({up[1], down[1], up[2], down[2], up[3], down[3], output_down[1], output_down[3]}),
    .born_rule(born_rules), .survival_rule(survival_rules), .clock(clock), .state(output_down[2]),
    .out_force(u2), .out_control(a2));
  \cell  cell_10 (
    .around({up[9], down[9], up[10], down[10], up[11], down[11], output_down[9], output_down[11]}),
    .born_rule(born_rules), .survival_rule(survival_rules), .clock(clock), .state(output_down[10]),
    .out_force(u10), .out_control(a10));
  \cell  cell_11 (
    .around({up[17], down[17], up[18], down[18], up[19], down[19], output_down[17], output_down[19]}),
    .born_rule(born_rules), .survival_rule(survival_rules), .clock(clock), .state(output_down[18]),
    .out_force(u18), .out_control(a18));
  \cell  cell_12 (
    .around({up[25], down[25], up[26], down[26], up[27], down[27], output_down[25], output_down[27]}),
    .born_rule(born_rules), .survival_rule(survival_rules), .clock(clock), .state(output_down[26]),
    .out_force(u26), .out_control(a26));
  \cell  cell_13 (
    .around({up[2], down[2], up[3], down[3], up[4], down[4], output_down[2], output_down[4]}),
    .born_rule(born_rules), .survival_rule(survival_rules), .clock(clock), .state(output_down[3]),
    .out_force(u3), .out_control(a3));
  \cell  cell_14 (
    .around({up[10], down[10], up[11], down[11], up[12], down[12], output_down[10], output_down[12]}),
    .born_rule(born_rules), .survival_rule(survival_rules), .clock(clock), .state(output_down[11]),
    .out_force(u11), .out_control(a11));
  \cell  cell_15 (
    .around({up[18], down[18], up[19], down[19], up[20], down[20], output_down[18], output_down[20]}),
    .born_rule(born_rules), .survival_rule(survival_rules), .clock(clock), .state(output_down[19]),
    .out_force(u19), .out_control(a19));
  \cell  cell_16 (
    .around({up[26], down[26], up[27], down[27], up[28], down[28], output_down[26], output_down[28]}),
    .born_rule(born_rules), .survival_rule(survival_rules), .clock(clock), .state(output_down[27]),
    .out_force(u27), .out_control(a27));
  \cell  cell_17 (
    .around({up[3], down[3], up[4], down[4], up[5], down[5], output_down[3], output_down[5]}),
    .born_rule(born_rules), .survival_rule(survival_rules), .clock(clock), .state(output_down[4]),
    .out_force(u4), .out_control(a4));
  \cell  cell_18 (
    .around({up[11], down[11], up[12], down[12], up[13], down[13], output_down[11], output_down[13]}),
    .born_rule(born_rules), .survival_rule(survival_rules), .clock(clock), .state(output_down[12]),
    .out_force(u12), .out_control(a12));
  \cell  cell_19 (
    .around({up[19], down[19], up[20], down[20], up[21], down[21], output_down[19], output_down[21]}),
    .born_rule(born_rules), .survival_rule(survival_rules), .clock(clock), .state(output_down[20]),
    .out_force(u20), .out_control(a20));
  \cell  cell_20 (
    .around({up[27], down[27], up[28], down[28], up[29], down[29], output_down[27], output_down[29]}),
    .born_rule(born_rules), .survival_rule(survival_rules), .clock(clock), .state(output_down[28]),
    .out_force(u28), .out_control(a28));
  \cell  cell_21 (
    .around({up[4], down[4], up[5], down[5], up[6], down[6], output_down[4], output_down[6]}),
    .born_rule(born_rules), .survival_rule(survival_rules), .clock(clock), .state(output_down[5]),
    .out_force(u5), .out_control(a5));
  \cell  cell_22 (
    .around({up[12], down[12], up[13], down[13], up[14], down[14], output_down[12], output_down[14]}),
    .born_rule(born_rules), .survival_rule(survival_rules), .clock(clock), .state(output_down[13]),
    .out_force(u13), .out_control(a13));
  \cell  cell_23 (
    .around({up[20], down[20], up[21], down[21], up[22], down[22], output_down[20], output_down[22]}),
    .born_rule(born_rules), .survival_rule(survival_rules), .clock(clock), .state(output_down[21]),
    .out_force(u21), .out_control(a21));
  \cell  cell_24 (
    .around({up[28], down[28], up[29], down[29], up[30], down[30], output_down[28], output_down[30]}),
    .born_rule(born_rules), .survival_rule(survival_rules), .clock(clock), .state(output_down[29]),
    .out_force(u29), .out_control(a29));
  \cell  cell_25 (
    .around({up[5], down[5], up[6], down[6], up[7], down[7], output_down[5], output_down[7]}),
    .born_rule(born_rules), .survival_rule(survival_rules), .clock(clock), .state(output_down[6]),
    .out_force(u6), .out_control(a6));
  \cell  cell_26 (
    .around({up[13], down[13], up[14], down[14], up[15], down[15], output_down[13], output_down[15]}),
    .born_rule(born_rules), .survival_rule(survival_rules), .clock(clock), .state(output_down[14]),
    .out_force(u14), .out_control(a14));
  \cell  cell_27 (
    .around({up[21], down[21], up[22], down[22], up[23], down[23], output_down[21], output_down[23]}),
    .born_rule(born_rules), .survival_rule(survival_rules), .clock(clock), .state(output_down[22]),
    .out_force(u22), .out_control(a22));
  \cell  cell_28 (
    .around({up[29], down[29], up[30], down[30], up[31], down[31], output_down[29], output_down[31]}),
    .born_rule(born_rules), .survival_rule(survival_rules), .clock(clock), .state(output_down[30]),
    .out_force(u30), .out_control(a30));
  \cell  cell_29 (
    .around({up[6], down[6], up[7], down[7], up[8], down[8], output_down[6], output_down[8]}),
    .born_rule(born_rules), .survival_rule(survival_rules), .clock(clock), .state(output_down[7]),
    .out_force(u7), .out_control(a7));
  \cell  cell_30 (
    .around({up[14], down[14], up[15], down[15], up[16], down[16], output_down[14], output_down[16]}),
    .born_rule(born_rules), .survival_rule(survival_rules), .clock(clock), .state(output_down[15]),
    .out_force(u15), .out_control(a15));
  \cell  cell_31 (
    .around({up[22], down[22], up[23], down[23], up[24], down[24], output_down[22], output_down[24]}),
    .born_rule(born_rules), .survival_rule(survival_rules), .clock(clock), .state(output_down[23]),
    .out_force(u23), .out_control(a23));
  \cell  cell_32 (
    .around({up[30], down[30], up[31], down[31], up[0], down[0], output_down[0], output_down[30]}),
    .born_rule(born_rules), .survival_rule(survival_rules), .clock(clock), .state(output_down[31]),
    .out_force(u31), .out_control(a31));

  assign output_main = output_down;
  assign output_up = output_down;

  // Other names for the same wires on the sheet: d3 = down[3]; p3 = up[3]; d11 = down[11]; p11 = up[11];
  //   d19 = down[19]; p19 = up[19]; d27 = down[27]; p27 = up[27]; d4 = down[4]; p4 = up[4]; d12 = down[12];
  //   p12 = up[12]; d20 = down[20]; p20 = up[20]; d28 = down[28]; p28 = up[28]; d5 = down[5]; p5 = up[5];
  //   d13 = down[13]; p13 = up[13]; d21 = down[21]; p21 = up[21]; d29 = down[29]; p29 = up[29]; d8 = down[8];
  //   p8 = up[8]; d7 = down[7]; p7 = up[7]; d6 = down[6]; p6 = up[6]; d16 = down[16]; p16 = up[16]; d15 = down[15];
  //   p15 = up[15]; d14 = down[14]; p14 = up[14]; d24 = down[24]; p24 = up[24]; d23 = down[23]; p23 = up[23];
  //   d22 = down[22]; p22 = up[22]; d0 = down[0]; p0 = up[0]; d31 = down[31]; p31 = up[31]; d30 = down[30];
  //   p30 = up[30]; bor[7:0] = born_rules; adr[4:0] = cell_adr[4:0]; cl = clock; d1 = down[1]; d2 = down[2];
  //   d9 = down[9]; d10 = down[10]; d17 = down[17]; d18 = down[18]; d25 = down[25]; d26 = down[26];
  //   m0 = output_down[0]; output[31:0] = output_down; m1 = output_down[1]; m2 = output_down[2]; m3 = output_down[3];
  //   m4 = output_down[4]; m5 = output_down[5]; m6 = output_down[6]; m7 = output_down[7]; m8 = output_down[8];
  //   m9 = output_down[9]; m10 = output_down[10]; m11 = output_down[11]; m12 = output_down[12]; m13 = output_down[13];
  //   m14 = output_down[14]; m15 = output_down[15]; m16 = output_down[16]; m17 = output_down[17];
  //   m18 = output_down[18]; m19 = output_down[19]; m20 = output_down[20]; m21 = output_down[21];
  //   m22 = output_down[22]; m23 = output_down[23]; m24 = output_down[24]; m25 = output_down[25];
  //   m26 = output_down[26]; m27 = output_down[27]; m28 = output_down[28]; m29 = output_down[29];
  //   m30 = output_down[30]; m31 = output_down[31]; sur[7:0] = survival_rules; p1 = up[1]; p2 = up[2]; p9 = up[9];
  //   p10 = up[10]; p17 = up[17]; p18 = up[18]; p25 = up[25]; p26 = up[26]
endmodule

module videobuffer (
  input  val,
  input  [7:0] sur,
  input  [7:0] born,
  input  cl,
  input  start_stop,
  input  update,
  input  [7:0] line_adr,
  input  [7:0] cell_adr,
  output [31:0] out_9,
  output [31:0] out_10,
  output [31:0] out_11,
  output [31:0] out_12,
  output [31:0] out_13,
  output [31:0] out_14,
  output [31:0] out_15,
  output [31:0] out_16,
  output [31:0] out_17,
  output [31:0] out_18,
  output [31:0] out_19,
  output [31:0] out_20,
  output [31:0] out_21,
  output [31:0] out_22,
  output [31:0] out_23,
  output [31:0] out_24,
  output [31:0] out_25,
  output [31:0] out_26,
  output [31:0] out_27,
  output [31:0] out_28,
  output [31:0] out_29,
  output [31:0] out_30,
  output [31:0] out_31,
  output [31:0] out_32,
  output [31:0] out_33,
  output [31:0] out_34,
  output [31:0] out_35,
  output [31:0] out_36,
  output [31:0] out_37,
  output [31:0] out_38,
  output [31:0] out_39,
  output [31:0] out_40
);

  wire a0, a1, a2, a3, a4, a5, a6, a7, a8, a9, a10, a11, a12, a13, a14, a15, a16, a17, a18, a19, a20, a21,
       a22, a23, a24, a25, a26, a27, a28, a29, a30, a31, and_1_out, controlled_buffer_1_out, not_1_out;
  wire [7:0] u0, u1, u2, u3, u4, u5, u6, u7, u8, u9, u10, u11, u12, u13, u14, u15, u16, u17, u18, u19, u20,
       u21, u22, u23, u24, u25, u26, u27, u28, u29, u30, u31;
  wire [31:0] c1, c2, line_1_output_down, line_2_output_down, line_2_output_up, line_3_output_down,
       line_3_output_up, line_4_output_down, line_4_output_up, line_5_output_down, line_5_output_up,
       line_6_output_down, line_6_output_up, line_7_output_down, line_7_output_up, line_8_output_down,
       line_8_output_up, line_9_output_down, line_9_output_up, line_10_output_down, line_10_output_up,
       line_11_output_down, line_11_output_up, line_12_output_down, line_12_output_up, line_13_output_down,
       line_13_output_up, line_14_output_down, line_14_output_up, line_15_output_down, line_15_output_up,
       line_16_output_down, line_16_output_up, line_17_output_down, line_17_output_up, line_18_output_down,
       line_18_output_up, line_19_output_down, line_19_output_up, line_20_output_down, line_20_output_up,
       line_21_output_down, line_21_output_up, line_22_output_down, line_22_output_up, line_23_output_down,
       line_23_output_up, line_24_output_down, line_24_output_up, line_25_output_down, line_25_output_up,
       line_26_output_down, line_26_output_up, line_27_output_down, line_27_output_up, line_28_output_down,
       line_28_output_up, line_29_output_down, line_29_output_up, line_30_output_down, line_30_output_up,
       line_31_output_down, line_31_output_up, line_32_output_up;

  line line_1 (
    .survival_rules(sur), .born_rules(born), .clock(controlled_buffer_1_out), .output_up(c1),
    .output_down(line_1_output_down), .up(c2), .cell_adr(u0), .down(line_2_output_up), .output_main(out_9),
    .ctrl(a0), .val(val));
  line line_2 (
    .survival_rules(sur), .born_rules(born), .clock(controlled_buffer_1_out), .output_up(line_2_output_up),
    .output_down(line_2_output_down), .up(line_1_output_down), .cell_adr(u1), .down(line_3_output_up),
    .output_main(out_10), .ctrl(a1), .val(val));
  line line_3 (
    .survival_rules(sur), .born_rules(born), .clock(controlled_buffer_1_out), .output_up(line_3_output_up),
    .output_down(line_3_output_down), .up(line_2_output_down), .cell_adr(u2), .down(line_4_output_up),
    .output_main(out_11), .ctrl(a2), .val(val));
  line line_4 (
    .survival_rules(sur), .born_rules(born), .clock(controlled_buffer_1_out), .output_up(line_4_output_up),
    .output_down(line_4_output_down), .up(line_3_output_down), .cell_adr(u3), .down(line_5_output_up),
    .output_main(out_12), .ctrl(a3), .val(val));
  line line_5 (
    .survival_rules(sur), .born_rules(born), .clock(controlled_buffer_1_out), .output_up(line_5_output_up),
    .output_down(line_5_output_down), .up(line_4_output_down), .cell_adr(u4), .down(line_6_output_up),
    .output_main(out_13), .ctrl(a4), .val(val));
  line line_6 (
    .survival_rules(sur), .born_rules(born), .clock(controlled_buffer_1_out), .output_up(line_6_output_up),
    .output_down(line_6_output_down), .up(line_5_output_down), .cell_adr(u5), .down(line_7_output_up),
    .output_main(out_14), .ctrl(a5), .val(val));
  line line_7 (
    .survival_rules(sur), .born_rules(born), .clock(controlled_buffer_1_out), .output_up(line_7_output_up),
    .output_down(line_7_output_down), .up(line_6_output_down), .cell_adr(u6), .down(line_8_output_up),
    .output_main(out_15), .ctrl(a6), .val(val));
  line line_8 (
    .survival_rules(sur), .born_rules(born), .clock(controlled_buffer_1_out), .output_up(line_8_output_up),
    .output_down(line_8_output_down), .up(line_7_output_down), .cell_adr(u7), .down(line_9_output_up),
    .output_main(out_16), .ctrl(a7), .val(val));
  line line_9 (
    .survival_rules(sur), .born_rules(born), .clock(controlled_buffer_1_out), .output_up(line_9_output_up),
    .output_down(line_9_output_down), .up(line_8_output_down), .cell_adr(u8), .down(line_10_output_up),
    .output_main(out_17), .ctrl(a8), .val(val));
  line line_10 (
    .survival_rules(sur), .born_rules(born), .clock(controlled_buffer_1_out), .output_up(line_10_output_up),
    .output_down(line_10_output_down), .up(line_9_output_down), .cell_adr(u9), .down(line_11_output_up),
    .output_main(out_18), .ctrl(a9), .val(val));
  line line_11 (
    .survival_rules(sur), .born_rules(born), .clock(controlled_buffer_1_out), .output_up(line_11_output_up),
    .output_down(line_11_output_down), .up(line_10_output_down), .cell_adr(u10), .down(line_12_output_up),
    .output_main(out_19), .ctrl(a10), .val(val));
  line line_12 (
    .survival_rules(sur), .born_rules(born), .clock(controlled_buffer_1_out), .output_up(line_12_output_up),
    .output_down(line_12_output_down), .up(line_11_output_down), .cell_adr(u11), .down(line_13_output_up),
    .output_main(out_20), .ctrl(a11), .val(val));
  line line_13 (
    .survival_rules(sur), .born_rules(born), .clock(controlled_buffer_1_out), .output_up(line_13_output_up),
    .output_down(line_13_output_down), .up(line_12_output_down), .cell_adr(u12), .down(line_14_output_up),
    .output_main(out_21), .ctrl(a12), .val(val));
  line line_14 (
    .survival_rules(sur), .born_rules(born), .clock(controlled_buffer_1_out), .output_up(line_14_output_up),
    .output_down(line_14_output_down), .up(line_13_output_down), .cell_adr(u13), .down(line_15_output_up),
    .output_main(out_22), .ctrl(a13), .val(val));
  line line_15 (
    .survival_rules(sur), .born_rules(born), .clock(controlled_buffer_1_out), .output_up(line_15_output_up),
    .output_down(line_15_output_down), .up(line_14_output_down), .cell_adr(u14), .down(line_16_output_up),
    .output_main(out_23), .ctrl(a14), .val(val));
  line line_16 (
    .survival_rules(sur), .born_rules(born), .clock(controlled_buffer_1_out), .output_up(line_16_output_up),
    .output_down(line_16_output_down), .up(line_15_output_down), .cell_adr(u15), .down(line_17_output_up),
    .output_main(out_24), .ctrl(a15), .val(val));
  line line_17 (
    .survival_rules(sur), .born_rules(born), .clock(controlled_buffer_1_out), .output_up(line_17_output_up),
    .output_down(line_17_output_down), .up(line_16_output_down), .cell_adr(u16), .down(line_18_output_up),
    .output_main(out_25), .ctrl(a16), .val(val));
  line line_18 (
    .survival_rules(sur), .born_rules(born), .clock(controlled_buffer_1_out), .output_up(line_18_output_up),
    .output_down(line_18_output_down), .up(line_17_output_down), .cell_adr(u17), .down(line_19_output_up),
    .output_main(out_26), .ctrl(a17), .val(val));
  line line_19 (
    .survival_rules(sur), .born_rules(born), .clock(controlled_buffer_1_out), .output_up(line_19_output_up),
    .output_down(line_19_output_down), .up(line_18_output_down), .cell_adr(u18), .down(line_20_output_up),
    .output_main(out_27), .ctrl(a18), .val(val));
  line line_20 (
    .survival_rules(sur), .born_rules(born), .clock(controlled_buffer_1_out), .output_up(line_20_output_up),
    .output_down(line_20_output_down), .up(line_19_output_down), .cell_adr(u19), .down(line_21_output_up),
    .output_main(out_28), .ctrl(a19), .val(val));
  line line_21 (
    .survival_rules(sur), .born_rules(born), .clock(controlled_buffer_1_out), .output_up(line_21_output_up),
    .output_down(line_21_output_down), .up(line_20_output_down), .cell_adr(u20), .down(line_22_output_up),
    .output_main(out_29), .ctrl(a20), .val(val));
  line line_22 (
    .survival_rules(sur), .born_rules(born), .clock(controlled_buffer_1_out), .output_up(line_22_output_up),
    .output_down(line_22_output_down), .up(line_21_output_down), .cell_adr(u21), .down(line_23_output_up),
    .output_main(out_30), .ctrl(a21), .val(val));
  line line_23 (
    .survival_rules(sur), .born_rules(born), .clock(controlled_buffer_1_out), .output_up(line_23_output_up),
    .output_down(line_23_output_down), .up(line_22_output_down), .cell_adr(u22), .down(line_24_output_up),
    .output_main(out_31), .ctrl(a22), .val(val));
  line line_24 (
    .survival_rules(sur), .born_rules(born), .clock(controlled_buffer_1_out), .output_up(line_24_output_up),
    .output_down(line_24_output_down), .up(line_23_output_down), .cell_adr(u23), .down(line_25_output_up),
    .output_main(out_32), .ctrl(a23), .val(val));
  line line_25 (
    .survival_rules(sur), .born_rules(born), .clock(controlled_buffer_1_out), .output_up(line_25_output_up),
    .output_down(line_25_output_down), .up(line_24_output_down), .cell_adr(u24), .down(line_26_output_up),
    .output_main(out_33), .ctrl(a24), .val(val));
  line line_26 (
    .survival_rules(sur), .born_rules(born), .clock(controlled_buffer_1_out), .output_up(line_26_output_up),
    .output_down(line_26_output_down), .up(line_25_output_down), .cell_adr(u25), .down(line_27_output_up),
    .output_main(out_34), .ctrl(a25), .val(val));
  line line_27 (
    .survival_rules(sur), .born_rules(born), .clock(controlled_buffer_1_out), .output_up(line_27_output_up),
    .output_down(line_27_output_down), .up(line_26_output_down), .cell_adr(u26), .down(line_28_output_up),
    .output_main(out_35), .ctrl(a26), .val(val));
  line line_28 (
    .survival_rules(sur), .born_rules(born), .clock(controlled_buffer_1_out), .output_up(line_28_output_up),
    .output_down(line_28_output_down), .up(line_27_output_down), .cell_adr(u27), .down(line_29_output_up),
    .output_main(out_36), .ctrl(a27), .val(val));
  line line_29 (
    .survival_rules(sur), .born_rules(born), .clock(controlled_buffer_1_out), .output_up(line_29_output_up),
    .output_down(line_29_output_down), .up(line_28_output_down), .cell_adr(u28), .down(line_30_output_up),
    .output_main(out_37), .ctrl(a28), .val(val));
  line line_30 (
    .survival_rules(sur), .born_rules(born), .clock(controlled_buffer_1_out), .output_up(line_30_output_up),
    .output_down(line_30_output_down), .up(line_29_output_down), .cell_adr(u29), .down(line_31_output_up),
    .output_main(out_38), .ctrl(a29), .val(val));
  line line_31 (
    .survival_rules(sur), .born_rules(born), .clock(controlled_buffer_1_out), .output_up(line_31_output_up),
    .output_down(line_31_output_down), .up(line_30_output_down), .cell_adr(u30), .down(line_32_output_up),
    .output_main(out_39), .ctrl(a30), .val(val));
  line line_32 (
    .survival_rules(sur), .born_rules(born), .clock(controlled_buffer_1_out), .output_up(line_32_output_up),
    .output_down(c2), .up(line_31_output_down), .cell_adr(u31), .down(c1), .output_main(out_40), .ctrl(a31),
    .val(val));
  assign controlled_buffer_1_out = and_1_out ? cl : 1'bz;  // Controlled_Buffer controlled_buffer_1
  Pull_Resistor pull_resistor_1 (.node(controlled_buffer_1_out));
  and and_1 (and_1_out, start_stop, not_1_out);
  Demultiplexer #(.select(5), .width(8), .enable("false")) demultiplexer_1 (
    .out0(u0), .out1(u1), .out2(u2), .out3(u3), .out4(u4), .out5(u5), .out6(u6), .out7(u7), .out8(u8),
    .out9(u9), .out10(u10), .out11(u11), .out12(u12), .out13(u13), .out14(u14), .out15(u15), .out16(u16),
    .out17(u17), .out18(u18), .out19(u19), .out20(u20), .out21(u21), .out22(u22), .out23(u23), .out24(u24),
    .out25(u25), .out26(u26), .out27(u27), .out28(u28), .out29(u29), .out30(u30), .out31(u31), .in(cell_adr),
    .sel(line_adr[4:0]));
  Demultiplexer #(.select(5), .enable("false")) demultiplexer_2 (
    .out0(a0), .out1(a1), .out2(a2), .out3(a3), .out4(a4), .out5(a5), .out6(a6), .out7(a7), .out8(a8),
    .out9(a9), .out10(a10), .out11(a11), .out12(a12), .out13(a13), .out14(a14), .out15(a15), .out16(a16),
    .out17(a17), .out18(a18), .out19(a19), .out20(a20), .out21(a21), .out22(a22), .out23(a23), .out24(a24),
    .out25(a25), .out26(a26), .out27(a27), .out28(a28), .out29(a29), .out30(a30), .out31(a31), .in(update),
    .sel(line_adr[4:0]));
  not not_1 (not_1_out, update);

  // Other names for the same wires on the sheet: ctrl = update; adr[4:0] = line_adr[4:0]; o0[31:0] = out_9;
  //   o1[31:0] = out_10; o2[31:0] = out_11; o3[31:0] = out_12; o4[31:0] = out_13; o5[31:0] = out_14;
  //   o6[31:0] = out_15; o7[31:0] = out_16; o8[31:0] = out_17; o9[31:0] = out_18; o10[31:0] = out_19;
  //   o11[31:0] = out_20; o12[31:0] = out_21; o13[31:0] = out_22; o14[31:0] = out_23; o15[31:0] = out_24;
  //   o16[31:0] = out_25; o17[31:0] = out_26; o18[31:0] = out_27; o19[31:0] = out_28; o20[31:0] = out_29;
  //   o21[31:0] = out_30; o22[31:0] = out_31; o23[31:0] = out_32; o24[31:0] = out_33; o25[31:0] = out_34;
  //   o26[31:0] = out_35; o27[31:0] = out_36; o28[31:0] = out_37; o29[31:0] = out_38; o30[31:0] = out_39;
  //   o31[31:0] = out_40
endmodule

module check_rules (
  input  [3:0] count,
  input  [7:0] born_rule,
  input  [7:0] survival_rule,
  output Born,
  output survive
);

  Multiplexer #(.select(4), .enable("false")) multiplexer_1 (
    .in0(1'b0), .in1(born_rule[0]), .in2(born_rule[1]), .in3(born_rule[2]), .in4(born_rule[3]),
    .in5(born_rule[4]), .in6(born_rule[5]), .in7(born_rule[6]), .in8(born_rule[7]), .out(Born), .sel(count));  // open: in9, in10, in11, in12, in13, in14, in15
  Multiplexer #(.select(4), .enable("false")) multiplexer_2 (
    .in0(1'b0), .in1(survival_rule[0]), .in2(survival_rule[1]), .in3(survival_rule[2]),
    .in4(survival_rule[3]), .in5(survival_rule[4]), .in6(survival_rule[5]), .in7(survival_rule[6]),
    .in8(survival_rule[7]), .out(survive), .sel(count));  // open: in9, in10, in11, in12, in13, in14, in15
endmodule

module ProcessorLogic (
  input  clock,
  input  [6:0] symb,
  input  kb_ready,
  output start_stop,
  output out_ctr,
  output [7:0] born,
  output [7:0] sur,
  output [7:0] line_addr,
  output [7:0] cell_addr,
  output val,
  output [6:0] ter_data,
  output ter_ctrl,
  output kb_ctrl
);

  wire and_3_out, and_4_out, and_5_out, and_6_out, and_7_out, and_8_out, and_9_out, and_10_out, and_11_out,
       cdm_16_1_p4, cdm_16_1_p5, cdm_16_1_p7, cdm_16_1_p8, cdm_16_1_p10, cdm_16_1_p12, cdm_16_1_p13,
       cdm_16_1_p14, cdm_16_1_p15, cdm_16_1_p16, cdm_16_1_p17, comparator_2_eq, comparator_3_eq,
       comparator_4_eq, comparator_5_eq, comparator_6_eq, comparator_7_eq, comparator_8_eq, comparator_9_eq,
       decoder_1_out0, decoder_1_out1, I_Osel, IAck, In_out, interruptarbiter_1_vec, IRQ, mem, nand_1_out,
       not_1_out, not_2_out, or_1_out, RAM, Rset, test, word;
  wire [0:0] register_1_q;
  wire [1:1] comparator_1_eq;
  wire [5:0] vec;
  wire [15:0] address_bus, bit_extender_2_out, cdm_16_1_p22, cdm_16_1_p23, data_bus;
  wire [15:1] register_2_q, register_3_q, register_8_q;
  wire [15:8] register_4_q, register_5_q, register_6_q, register_7_q;

  // Probe on vec
  // Probe on cdm_16_1_p14
  // Probe on cdm_16_1_p13
  // Probe on cdm_16_1_p12
  // Probe on cdm_16_1_p10
  // Probe on cdm_16_1_p8
  // Probe on cdm_16_1_p7
  // Probe on cdm_16_1_p5
  // Probe on cdm_16_1_p4
  // CdM_16 cdm_16_1: pin names not known; wires that end beside it: IRQ, vec, IAck, cdm_16_1_p4, cdm_16_1_p5, clock, cdm_16_1_p7, cdm_16_1_p8, clock, cdm_16_1_p10, test, cdm_16_1_p12, cdm_16_1_p13, cdm_16_1_p14, cdm_16_1_p15, cdm_16_1_p16, cdm_16_1_p17, mem, In_out, word, address_bus, cdm_16_1_p22, cdm_16_1_p23
  not not_1 (not_1_out, nand_1_out);
  and and_1 (I_Osel, not_1_out, clock, mem);
  Bit_Extender #(.in_width(16), .out_width(7)) bit_extender_1 (.in(data_bus), .out(ter_data));
  // Probe on cdm_16_1_p15
  // Probe on cdm_16_1_p16
  // Probe on cdm_16_1_p17
  and and_2 (RAM, nand_1_out, mem);
  Comparator comparator_1 (.a(address_bus[7:0]), .b(8'h2), .eq(comparator_1_eq[1]));  // open: gt, lt
  Comparator comparator_2 (.a(address_bus[7:0]), .b({8{1'b0}}), .eq(comparator_2_eq));  // open: gt, lt
  assign data_bus = not_2_out ? cdm_16_1_p22 : 16'bz;  // Controlled_Buffer controlled_buffer_1
  not not_2 (not_2_out, In_out);
  assign cdm_16_1_p23 = In_out ? data_bus : 16'bz;  // Controlled_Buffer controlled_buffer_2
  nand nand_1 (nand_1_out, address_bus[8], address_bus[9], address_bus[10], address_bus[11], address_bus[12], address_bus[13], address_bus[14], address_bus[15]);
  or or_1 (or_1_out, comparator_1_eq[1], comparator_2_eq);
  assign data_bus = kb_ctrl ? bit_extender_2_out : 16'bz;  // Controlled_Buffer controlled_buffer_3
  assign data_bus = decoder_1_out1 ? {kb_ready, {14{1'b0}}, register_1_q[0]} : 16'bz;  // Controlled_Buffer controlled_buffer_4
  Register #(.width(1), .trigger("falling")) register_1 (
    .D(data_bus[0]), .en(decoder_1_out0), .Q(register_1_q[0]), .clk(clock), .clr(Rset));
  and and_3 (and_3_out, or_1_out, I_Osel);
  Decoder #(.select(2), .disabled(0)) decoder_1 (
    .out0(decoder_1_out0), .out1(decoder_1_out1), .out2(ter_ctrl), .out3(kb_ctrl),
    .sel({comparator_1_eq[1], In_out}), .en(and_3_out));
  assign bit_extender_2_out = {{9{1'b0}}, symb};  // Bit_Extender bit_extender_2
  // Debugger debugger_1: pin names not known; wires that end beside it: test
  // Probe on address_bus
  assign vec = interruptarbiter_1_vec ? 6'b000101 : 6'bz;  // Controlled_Buffer controlled_buffer_5
  and and_4 (and_4_out, kb_ready, register_1_q[0]);
  InterruptArbiter interruptarbiter_1 (
    .IReq_2(IRQ), .IAck(IAck), .IReq(1'b0), .vec(interruptarbiter_1_vec), .req(and_4_out), .done(kb_ctrl),
    .clock(clock));  // open: IAck_2
  // Probe on data_bus
  // RAM ram_1: pin names not known; wires that end beside it: address_bus, word, RAM, mem, clock, In_out, Rset, data_bus
  Button button_1 (.out(Rset));
  // Probe on data_bus
  Comparator comparator_3 (.a(address_bus[7:0]), .b(8'h4), .eq(comparator_3_eq));  // open: gt, lt
  and and_5 (and_5_out, comparator_3_eq, I_Osel);
  Comparator comparator_4 (.a(address_bus[7:0]), .b(8'h6), .eq(comparator_4_eq));  // open: gt, lt
  and and_6 (and_6_out, comparator_4_eq, I_Osel);
  Comparator comparator_5 (.a(address_bus[7:0]), .b(8'h8), .eq(comparator_5_eq));  // open: gt, lt
  and and_7 (and_7_out, comparator_5_eq, I_Osel);
  Comparator comparator_6 (.a(address_bus[7:0]), .b(8'ha), .eq(comparator_6_eq));  // open: gt, lt
  and and_8 (and_8_out, comparator_6_eq, I_Osel);
  Comparator comparator_7 (.a(address_bus[7:0]), .b(8'hc), .eq(comparator_7_eq));  // open: gt, lt
  and and_9 (and_9_out, comparator_7_eq, I_Osel);
  Comparator comparator_8 (.a(address_bus[7:0]), .b(8'he), .eq(comparator_8_eq));  // open: gt, lt
  and and_10 (and_10_out, comparator_8_eq, I_Osel);
  Comparator comparator_9 (.a(address_bus[7:0]), .b(8'h10), .eq(comparator_9_eq));  // open: gt, lt
  and and_11 (and_11_out, comparator_9_eq, I_Osel);
  Register #(.width(16), .trigger("falling")) register_2 (
    .D(data_bus), .en(and_5_out), .Q({register_2_q, start_stop}), .clk(clock), .clr(Rset));
  Register #(.width(16), .trigger("falling")) register_3 (
    .D(data_bus), .en(and_6_out), .Q({register_3_q, out_ctr}), .clk(clock), .clr(Rset));
  Register #(.width(16), .trigger("falling")) register_4 (
    .D(data_bus), .en(and_7_out), .Q({register_4_q, born}), .clk(clock), .clr(Rset));
  Register #(.width(16), .trigger("falling")) register_5 (
    .D(data_bus), .en(and_8_out), .Q({register_5_q, sur}), .clk(clock), .clr(Rset));
  Register #(.width(16), .trigger("falling")) register_6 (
    .D(data_bus), .en(and_9_out), .Q({register_6_q, line_addr}), .clk(clock), .clr(Rset));
  Register #(.width(16), .trigger("falling")) register_7 (
    .D(data_bus), .en(and_10_out), .Q({register_7_q, cell_addr}), .clk(clock), .clr(Rset));
  Register #(.width(16), .trigger("falling")) register_8 (
    .D(data_bus), .en(and_11_out), .Q({register_8_q, val}), .clk(clock), .clr(Rset));

  // Other names for the same wires on the sheet: read = In_out; I_Oadr[7:0] = address_bus[7:0]; cl = clock;
  //   I_Odat[15:0] = data_bus

  // Notes on the sheet:
  //   r7/fp
  //   r6
  //   r5
  //   r4
  //   r3
  //   r2
  //   r1
  //   r0
  //   memory-mapped I/O
  //   pc
  //   sp
  //   ps
  //   start/stop
  //   out_ctr
  //   born
  //   sur
  //   line_addr
  //   cell_addr
  //   val
endmodule

module InterruptArbiter (
  input  IReq,
  input  IAck,
  input  clock,
  input  req,
  input  done,
  output vec,
  output IReq_2,
  output IAck_2
);

  wire _00_out, _01_2_out, _01_out, _10_out, or_2_out;
  wire [1:0] nor_1_out, register_1_q;

  or or_1 (IReq_2, IReq, register_1_q[0]);
  and _01 (_01_out, ~register_1_q[1], register_1_q[0]);  // AND_Gate
  and and_1 (vec, _01_out, IAck);
  and and_2 (IAck_2, IAck, ~_01_out);  // AND_Gate
  and _00 (_00_out, req, ~register_1_q[0], ~register_1_q[1]);  // AND_Gate
  and _01_2 (_01_2_out, IAck, register_1_q[0], ~register_1_q[1]);  // AND_Gate
  or or_2 (or_2_out, _00_out, _01_2_out, _10_out);
  and _10 (_10_out, done, ~register_1_q[0], register_1_q[1]);  // AND_Gate
  Register #(.width(2), .trigger("falling")) register_1 (
    .D(nor_1_out), .en(or_2_out), .Q(register_1_q), .clk(clock));  // open: clr
  nor nor_1 (nor_1_out[0], register_1_q[0], register_1_q[1]);
  and and_3 (nor_1_out[1], register_1_q[0], ~register_1_q[1]);  // AND_Gate

  // Notes on the sheet:
  //   Req
  //   Ack
  //   done
  //   0->1->2->0
endmodule

module RS (
  input  S,
  input  R,
  output Q_prime,
  output Q
);

  Pull_Resistor pull_resistor_1 (.node(S));
  Pull_Resistor pull_resistor_2 (.node(R));
  nor nor_1 (Q_prime, S, Q);
  nor nor_2 (Q, Q_prime, R);
endmodule
